// Logisim project alu.circ as structural Verilog: 1 circuit, main circuit main
module main (
  input  [2:0] in_1,
  input  [31:0] X,
  input  [2:0] in_3,
  input  [31:0] Y,
  input  [3:0] Switch,
  output Signed_Overflow,
  output [2:0] out,
  output Equal,
  output [31:0] Result
);

  wire add_overflow, and_2_out, comparator_1_lt, comparator_2_lt, sub_overflow, xnor_1_out, xnor_2_out,
       xor_1_out, xor_2_out;
  wire [4:0] bit_extender_1_out, bit_extender_2_out, bit_extender_3_out;
  wire [31:0] add, addu, \and , \or , sll, slt, sltu, sra, srl, sub, subu;

  Shifter #(.width(32)) shifter_1 (.in(Y), .\dist (bit_extender_1_out), .out(sll));
  Bit_Extender #(.in_width(32), .out_width(5)) bit_extender_1 (.in(X), .out(bit_extender_1_out));
  Shifter #(.width(32), .shift("lr")) shifter_2 (.in(Y), .\dist (bit_extender_2_out), .out(srl));
  Bit_Extender #(.in_width(32), .out_width(5)) bit_extender_2 (.in(X), .out(bit_extender_2_out));
  Shifter #(.width(32), .shift("ar")) shifter_3 (.in(Y), .\dist (bit_extender_3_out), .out(sra));
  Bit_Extender #(.in_width(32), .out_width(5)) bit_extender_3 (.in(X), .out(bit_extender_3_out));
  Adder #(.width(32)) adder_1 (.a(X), .b(Y), .out(add));  // open: cin, cout
  Subtractor #(.width(32)) subtractor_1 (.a(X), .b(Y), .out(sub));  // open: bin, bout
  Adder #(.width(32)) adder_2 (.a(X), .b(Y), .out(addu));  // open: cin, cout
  Subtractor #(.width(32)) subtractor_2 (.a(X), .b(Y), .out(subu));  // open: bin, bout
  assign \and  = X & Y;  // AND_Gate and_1, 32 bits wide
  assign \or  = X | Y;  // OR_Gate or_1, 32 bits wide
  Comparator #(.width(32)) comparator_1 (.a(X), .b(Y), .lt(comparator_1_lt));  // open: gt, eq
  Comparator #(.width(32), .mode("unsigned")) comparator_2 (.a(X), .b(Y), .lt(comparator_2_lt));  // open: gt, eq
  xnor xnor_1 (xnor_1_out, X[31], Y[31]);
  and and_2 (and_2_out, X[31], Y[31]);
  xor xor_1 (xor_1_out, and_2_out, add[31]);
  xor xor_2 (xor_2_out, X[31], Y[31]);
  assign slt = {{31{1'b0}}, comparator_1_lt};  // Bit_Extender bit_extender_4
  assign sltu = {{31{1'b0}}, comparator_2_lt};  // Bit_Extender bit_extender_5
  and and_3 (add_overflow, xnor_1_out, xor_1_out);
  and and_4 (sub_overflow, xor_2_out, xnor_2_out);
  xnor xnor_2 (xnor_2_out, Y[31], sub[31]);
  Adder #(.width(3)) adder_3 (.a(in_1), .b(in_3), .out(out));  // open: cin, cout
  Comparator #(.width(32)) comparator_3 (.a(X), .b(Y), .eq(Equal));  // open: gt, lt
  Multiplexer #(.select(4), .width(32)) multiplexer_1 (
    .in0(sll), .in1(srl), .in2(sra), .in5(add), .in6(addu), .in7(sub), .in8(subu), .in9(\and ), .in10(\or ),
    .in11(slt), .in12(sltu), .out(Result), .sel(Switch));  // open: in3, in4, in13, in14, in15, en
  Multiplexer #(.select(4)) multiplexer_2 (
    .in0(1'b0), .in1(1'b0), .in2(1'b0), .in3(1'b0), .in4(1'b0), .in5(add_overflow), .in6(1'b0),
    .in7(sub_overflow), .in8(1'b0), .in9(1'b0), .in10(1'b0), .in11(1'b0), .in12(1'b0), .in13(1'b0),
    .in14(1'b0), .in15(1'b0), .out(Signed_Overflow), .sel(Switch));  // open: en

  // Other names for the same wires on the sheet: overflow = Signed_Overflow; S[3:0] = Switch

  // Notes on the sheet:
  //   INPUTS to your circuit
  //   DON'T CHANGE THE LOCATIONS OF THE INPUTS AND OUTPUTS!
  //   OUTPUTS from your circuit
endmodule
