// Logisim project cpu.circ as structural Verilog: 2 circuits, main circuit main
module main (
  input  [31:0] INSTRUCTION,
  input  CLOCK,
  output [31:0] FETCH_ADDRESS,
  output [31:0] s0_Value,
  output [31:0] s1_Value,
  output [31:0] s2_Value,
  output [31:0] ra_Value,
  output [31:0] sp_Value
);

  wire ALUSrc, and_1_out, and_2_out, Branch, BranchNE, BranchPass, ExtOp, Jal, Jr, Jump, LUI, main_2_equal,
       main_2_signed_overflow, MemToReg, MemWrite, not_1_out, or_1_out, RegDst, RegWrite, Shift;
  wire [3:0] ALUCtr;
  wire [4:0] multiplexer_4_out, multiplexer_5_out;
  wire [5:0] funct, opcode;
  wire [25:6] JumpAddr;
  wire [27:0] bit_extender_2_out, shifter_1_out;
  wire [31:0] adder_1_out, adder_2_out, bit_extender_3_out, bit_extender_4_out, main_1_read_data_1,
       main_1_read_data_2, main_2_result, main_3_p5, multiplexer_1_out, multiplexer_2_out, multiplexer_3_out,
       multiplexer_6_out, multiplexer_7_out, multiplexer_8_out, multiplexer_9_out, multiplexer_10_out,
       multiplexer_11_out, shamt, shftamt, shifter_2_out;

  Multiplexer #(.width(32)) multiplexer_1 (
    .in0(multiplexer_10_out), .in1({adder_1_out[31:28], shifter_1_out}), .out(multiplexer_1_out), .sel(Jump));  // open: en
  Multiplexer #(.width(32)) multiplexer_2 (
    .in0(INSTRUCTION), .in1({32{1'b0}}), .out(multiplexer_2_out), .sel(or_1_out));  // open: en
  or or_1 (or_1_out, Jump, BranchPass);
  Multiplexer #(.width(32)) multiplexer_3 (
    .in0(multiplexer_1_out), .in1(ra_Value), .out(multiplexer_3_out), .sel(Jr));  // open: en
  assign shamt = {{27{1'b0}}, JumpAddr[10:6]};  // Bit_Extender bit_extender_1
  Register #(.width(32)) register_1 (
    .D(multiplexer_2_out), .Q({opcode, JumpAddr, funct}), .clk(CLOCK));  // open: en, clr
  assign bit_extender_2_out = {{2{1'b0}}, {JumpAddr, funct}};  // Bit_Extender bit_extender_2
  Register #(.width(32)) PC (.D(multiplexer_3_out), .Q(FETCH_ADDRESS), .clk(CLOCK));  // open: en, clr
  Multiplexer #(.width(5)) multiplexer_4 (
    .in0(JumpAddr[20:16]), .in1(JumpAddr[15:11]), .out(multiplexer_4_out), .sel(RegDst));  // open: en
  Multiplexer #(.width(5)) multiplexer_5 (
    .in0(multiplexer_4_out), .in1({5{1'b1}}), .out(multiplexer_5_out), .sel(Jal));  // open: en
  assign bit_extender_3_out = {{16{1'b0}}, {JumpAddr[15:6], funct}};  // Bit_Extender bit_extender_3
  assign bit_extender_4_out = {{16{JumpAddr[15]}}, {JumpAddr[15:6], funct}};  // Bit_Extender bit_extender_4
  Shifter #(.width(28)) shifter_1 (.in(bit_extender_2_out), .\dist (5'b00010), .out(shifter_1_out));
  Adder #(.width(32)) adder_1 (.a(FETCH_ADDRESS), .b(32'h4), .out(adder_1_out));  // open: cin, cout
  Multiplexer #(.width(32)) multiplexer_6 (
    .in0(multiplexer_11_out), .in1(FETCH_ADDRESS), .out(multiplexer_6_out), .sel(Jal));  // open: en
  Multiplexer #(.width(32)) multiplexer_7 (
    .in0(bit_extender_3_out), .in1(bit_extender_4_out), .out(multiplexer_7_out), .sel(ExtOp));  // open: en
  regfile_main main_1 (
    .Read_Register_1(JumpAddr[25:21]), .Read_Register_2(JumpAddr[20:16]), .Write_Register(multiplexer_5_out),
    .Write_Data(multiplexer_6_out), .Write_Enable(RegWrite), .Clock(CLOCK), .Read_Data_1(main_1_read_data_1),
    .Read_Data_2(main_1_read_data_2), .s0_Value(s0_Value), .s1_Value(s1_Value), .s2_Value(s2_Value),
    .ra_Value(ra_Value), .sp_Value(sp_Value));
  Shifter #(.width(32)) shifter_2 (.in(multiplexer_7_out), .\dist (5'b00010), .out(shifter_2_out));
  LED led_1 (.in(main_2_signed_overflow));
  Multiplexer #(.width(32)) multiplexer_8 (
    .in0(main_1_read_data_1), .in1(shftamt), .out(multiplexer_8_out), .sel(Shift));  // open: en
  alu_main main_2 (
    .Switch(ALUCtr), .X(multiplexer_8_out), .Equal(main_2_equal), .Result(main_2_result),
    .Signed_Overflow(main_2_signed_overflow), .Y(multiplexer_9_out));
  Multiplexer #(.width(32)) multiplexer_9 (
    .in0(main_1_read_data_2), .in1(multiplexer_7_out), .out(multiplexer_9_out), .sel(ALUSrc));  // open: en
  or or_2 (BranchPass, and_1_out, and_2_out);
  Multiplexer #(.width(32)) multiplexer_10 (
    .in0(adder_1_out), .in1(adder_2_out), .out(multiplexer_10_out), .sel(BranchPass));  // open: en
  Adder #(.width(32)) adder_2 (.a(FETCH_ADDRESS), .b(shifter_2_out), .out(adder_2_out));  // open: cin, cout
  and and_1 (and_1_out, BranchNE, not_1_out);
  not not_1 (not_1_out, main_2_equal);
  and and_2 (and_2_out, Branch, main_2_equal);
  // mem_main main_3: pin names not known; wires that end beside it: main_2_result, main_1_read_data_2, MemWrite, CLOCK, main_3_p5
  Multiplexer #(.width(32)) multiplexer_11 (
    .in0(main_2_result), .in1(main_3_p5), .out(multiplexer_11_out), .sel(MemToReg));  // open: en
  Multiplexer #(.width(32)) multiplexer_12 (.in0(shamt), .in1(32'h10), .out(shftamt), .sel(LUI));  // open: en
  Control_Unit control_unit_1 (
    .opcode(opcode), .funct(funct), .RegDst(RegDst), .ALUSrc(ALUSrc), .MemToReg(MemToReg),
    .RegWrite(RegWrite), .MemWrite(MemWrite), .Branch(Branch), .Jump(Jump), .ExtOp(ExtOp), .ALUCtr(ALUCtr),
    .Shift(Shift), .Jal(Jal), .Jr(Jr), .BranchNE(BranchNE), .LUI(LUI));

  // Other names for the same wires on the sheet: JumpAddr[5:0] = funct; clk = CLOCK; fetch_addr[31:0] = FETCH_ADDRESS;
  //   ra[31:0] = ra_Value; s0[31:0] = s0_Value; s1[31:0] = s1_Value; s2[31:0] = s2_Value; sp[31:0] = sp_Value

  // Notes on the sheet:
  //   Output
  //   These are outputs/inputs from run.circ
  //   Inputs
  //   These are DEBUG/TEST outputs from your circuit.
endmodule

module Control_Unit (
  input  [5:0] opcode,
  input  [5:0] funct,
  output RegDst,
  output ALUSrc,
  output MemToReg,
  output RegWrite,
  output MemWrite,
  output Branch,
  output Jump,
  output ExtOp,
  output [3:0] ALUCtr,
  output Shift,
  output Jal,
  output Jr,
  output BranchNE,
  output LUI
);

  wire and_2_out, and_3_out, and_4_out, and_5_out, and_6_out, and_7_out, and_8_out, and_9_out, and_10_out,
       and_11_out, and_12_out, and_13_out, and_14_out, and_15_out, and_16_out, and_17_out, and_18_out,
       and_19_out, and_20_out, and_21_out, and_22_out, and_23_out, comparator_2_eq, comparator_3_eq,
       comparator_4_eq, comparator_5_eq, comparator_6_eq, comparator_7_eq, comparator_8_eq, comparator_9_eq,
       comparator_10_eq, comparator_11_eq, comparator_12_eq, comparator_13_eq, comparator_14_eq,
       comparator_15_eq, comparator_16_eq, comparator_17_eq, comparator_18_eq, comparator_19_eq,
       comparator_20_eq, comparator_21_eq, comparator_22_eq, comparator_23_eq, comparator_24_eq,
       comparator_25_eq, comparator_26_eq, comparator_27_eq, comparator_28_eq, comparator_29_eq,
       comparator_30_eq, comparator_31_eq, comparator_34_eq, comparator_35_eq, comparator_36_eq,
       comparator_37_eq, comparator_39_eq, comparator_40_eq, comparator_41_eq, comparator_42_eq,
       comparator_43_eq, I_Type, not_1_out, not_2_out, not_3_out, not_4_out, not_5_out, or_1_out, or_2_out,
       or_3_out, or_4_out, or_5_out, or_6_out, or_7_out, or_8_out, or_9_out, or_10_out, or_11_out, or_12_out,
       or_13_out, R_Type, sw, swinc, undriven;

  not not_1 (not_1_out, Jump);
  not not_2 (not_2_out, R_Type);
  Comparator #(.width(6)) comparator_1 (.a(opcode), .b({6{1'b0}}), .eq(R_Type));  // open: gt, lt
  and and_1 (I_Type, not_1_out, not_2_out);
  and and_2 (and_2_out, R_Type, Jump);
  and and_3 (and_3_out, R_Type, not_3_out);
  Multiplexer multiplexer_1 (.in1(1'b1), .out(RegDst), .sel(R_Type));  // open: in0, en
  Multiplexer multiplexer_2 (.in1(1'b0), .out(RegWrite), .sel(and_2_out));  // open: in0, en
  Multiplexer multiplexer_3 (.in1(1'b1), .out(RegWrite), .sel(and_3_out));  // open: in0, en
  not not_3 (not_3_out, Jump);
  Comparator #(.width(6)) comparator_2 (.a(opcode), .b(6'b001100), .eq(comparator_2_eq));  // open: gt, lt
  Comparator #(.width(6)) comparator_3 (.a(opcode), .b(6'b001101), .eq(comparator_3_eq));  // open: gt, lt
  Comparator #(.width(6)) comparator_4 (.a(opcode), .b(6'b000100), .eq(comparator_4_eq));  // open: gt, lt
  Comparator #(.width(6)) comparator_5 (.a(opcode), .b(6'b000101), .eq(comparator_5_eq));  // open: gt, lt
  Comparator #(.width(6)) comparator_6 (.a(opcode), .b(6'b001100), .eq(comparator_6_eq));  // open: gt, lt
  Comparator #(.width(6)) comparator_7 (.a(opcode), .b(6'b001101), .eq(comparator_7_eq));  // open: gt, lt
  Comparator #(.width(6)) comparator_8 (.a(opcode), .b(6'b000100), .eq(comparator_8_eq));  // open: gt, lt
  Comparator #(.width(6)) comparator_9 (.a(opcode), .b(6'b000101), .eq(comparator_9_eq));  // open: gt, lt
  and and_4 (and_4_out, I_Type, sw);
  and and_5 (and_5_out, I_Type, not_5_out);
  not not_4 (not_4_out, or_1_out);
  or or_1 (or_1_out, comparator_2_eq, comparator_3_eq, comparator_4_eq, comparator_5_eq);
  or or_2 (or_2_out, comparator_6_eq, comparator_7_eq, comparator_8_eq, comparator_9_eq);
  Multiplexer multiplexer_4 (.in0(1'b0), .in1(1'b1), .out(ALUSrc), .sel(I_Type));  // open: en
  Multiplexer multiplexer_5 (.in1(1'b0), .out(RegDst), .sel(I_Type));  // open: in0, en
  Multiplexer multiplexer_6 (.in1(1'b0), .out(RegWrite), .sel(and_4_out));  // open: in0, en
  Multiplexer multiplexer_7 (.in1(1'b1), .out(RegWrite), .sel(and_5_out));  // open: in0, en
  not not_5 (not_5_out, sw);
  Multiplexer multiplexer_8 (.in1(1'b1), .out(ExtOp), .sel(and_6_out));  // open: in0, en
  and and_6 (and_6_out, ALUSrc, not_4_out);
  Multiplexer multiplexer_9 (.in1(1'b0), .out(ExtOp), .sel(and_7_out));  // open: in0, en
  and and_7 (and_7_out, ALUSrc, or_2_out);
  Comparator #(.width(6)) comparator_10 (.a(funct), .b(6'b001000), .eq(comparator_10_eq));  // open: gt, lt
  Multiplexer multiplexer_10 (.in0(1'b0), .in1(1'b1), .out(Jump), .sel(or_3_out));  // open: en
  or or_3 (or_3_out, and_8_out, comparator_11_eq, comparator_12_eq);
  and and_8 (and_8_out, R_Type, comparator_10_eq);
  Comparator #(.width(6)) comparator_11 (.a(opcode), .b(6'b000010), .eq(comparator_11_eq));  // open: gt, lt
  Comparator #(.width(6)) comparator_12 (.a(opcode), .b(6'b000011), .eq(comparator_12_eq));  // open: gt, lt
  Multiplexer multiplexer_11 (.in0(undriven), .in1(1'b1), .out(RegWrite), .sel(and_9_out));  // open: en
  and and_9 (and_9_out, Jump, comparator_13_eq);
  Comparator #(.width(6)) comparator_13 (.a(opcode), .b(6'b000011), .eq(comparator_13_eq));  // open: gt, lt
  Multiplexer multiplexer_12 (.in0(1'b0), .in1(1'b1), .out(Jal), .sel(and_10_out));  // open: en
  and and_10 (and_10_out, Jump, comparator_14_eq);
  Comparator #(.width(6)) comparator_14 (.a(opcode), .b(6'b000011), .eq(comparator_14_eq));  // open: gt, lt
  Comparator #(.width(6)) comparator_15 (.a(funct), .b(6'b100000), .eq(comparator_15_eq));  // open: gt, lt
  and and_11 (and_11_out, comparator_15_eq, R_Type);
  Comparator #(.width(6)) comparator_16 (.a(opcode), .b(6'b001000), .eq(comparator_16_eq));  // open: gt, lt
  Comparator #(.width(6)) comparator_17 (.a(funct), .b(6'b100001), .eq(comparator_17_eq));  // open: gt, lt
  and and_12 (and_12_out, comparator_17_eq, R_Type);
  Comparator #(.width(6)) comparator_18 (.a(opcode), .b(6'b001001), .eq(comparator_18_eq));  // open: gt, lt
  Comparator #(.width(6)) comparator_19 (.a(opcode), .b(6'b101011), .eq(comparator_19_eq));  // open: gt, lt
  Comparator #(.width(6)) comparator_20 (.a(opcode), .b(6'b100011), .eq(comparator_20_eq));  // open: gt, lt
  Comparator #(.width(6)) comparator_21 (.a(funct), .b(6'b100010), .eq(comparator_21_eq));  // open: gt, lt
  and and_13 (and_13_out, comparator_21_eq, R_Type);
  Comparator #(.width(6)) comparator_22 (.a(funct), .b(6'b100011), .eq(comparator_22_eq));  // open: gt, lt
  and and_14 (and_14_out, comparator_22_eq, R_Type);
  and and_15 (and_15_out, R_Type, comparator_23_eq);
  Comparator #(.width(6)) comparator_23 (.a(funct), .b(6'b001000), .eq(comparator_23_eq));  // open: gt, lt
  Multiplexer #(.width(4)) multiplexer_13 (.in1(4'b0101), .out(ALUCtr), .sel(or_4_out));  // open: in0, en
  or or_4 (or_4_out, and_11_out, comparator_16_eq);
  Multiplexer #(.width(4)) multiplexer_14 (.in1(4'b0110), .out(ALUCtr), .sel(or_5_out));  // open: in0, en
  or or_5 (or_5_out, and_12_out, comparator_18_eq, comparator_19_eq, comparator_20_eq);
  Multiplexer #(.width(4)) multiplexer_15 (.in1(4'b0111), .out(ALUCtr), .sel(and_13_out));  // open: in0, en
  Multiplexer #(.width(4)) multiplexer_16 (.in1(4'b1000), .out(ALUCtr), .sel(and_14_out));  // open: in0, en
  Multiplexer multiplexer_17 (.in0(1'b0), .in1(1'b1), .out(Branch), .sel(comparator_24_eq));  // open: en
  Comparator #(.width(6)) comparator_24 (.a(opcode), .b(6'b000100), .eq(comparator_24_eq));  // open: gt, lt
  Multiplexer multiplexer_18 (.in0(1'b0), .in1(1'b1), .out(BranchNE), .sel(comparator_25_eq));  // open: en
  Comparator #(.width(6)) comparator_25 (.a(opcode), .b(6'b000101), .eq(comparator_25_eq));  // open: gt, lt
  Multiplexer multiplexer_19 (.in0(1'b0), .in1(1'b1), .out(Jr), .sel(and_15_out));  // open: en
  Comparator #(.width(6)) comparator_26 (.a(funct), .b(6'b100100), .eq(comparator_26_eq));  // open: gt, lt
  Comparator #(.width(6)) comparator_27 (.a(opcode), .b(6'b001100), .eq(comparator_27_eq));  // open: gt, lt
  Comparator #(.width(6)) comparator_28 (.a(funct), .b(6'b101010), .eq(comparator_28_eq));  // open: gt, lt
  Comparator #(.width(6)) comparator_29 (.a(opcode), .b(6'b001010), .eq(comparator_29_eq));  // open: gt, lt
  Comparator #(.width(6)) comparator_30 (.a(funct), .b(6'b101011), .eq(comparator_30_eq));  // open: gt, lt
  Comparator #(.width(6)) comparator_31 (.a(opcode), .b(6'b001011), .eq(comparator_31_eq));  // open: gt, lt
  Comparator #(.width(6)) comparator_32 (.a(opcode), .b(6'b101011), .eq(sw));  // open: gt, lt
  Comparator #(.width(6)) comparator_33 (.a(opcode), .b(6'b101100), .eq(swinc));  // open: gt, lt
  Comparator #(.width(6)) comparator_34 (.a(opcode), .b(6'b100011), .eq(comparator_34_eq));  // open: gt, lt
  and and_16 (and_16_out, comparator_26_eq, R_Type);
  and and_17 (and_17_out, comparator_28_eq, R_Type);
  and and_18 (and_18_out, comparator_30_eq, R_Type);
  Multiplexer multiplexer_20 (.in0(1'b0), .in1(1'b1), .out(MemWrite), .sel(or_6_out));  // open: en
  or or_6 (or_6_out, sw, swinc);
  Multiplexer multiplexer_21 (.in0(1'b0), .in1(1'b1), .out(MemToReg), .sel(comparator_34_eq));  // open: en
  Multiplexer #(.width(4)) multiplexer_22 (.in1(4'b1001), .out(ALUCtr), .sel(or_7_out));  // open: in0, en
  or or_7 (or_7_out, and_16_out, comparator_27_eq);
  Multiplexer #(.width(4)) multiplexer_23 (.in1(4'b1011), .out(ALUCtr), .sel(or_8_out));  // open: in0, en
  or or_8 (or_8_out, and_17_out, comparator_29_eq);
  Multiplexer #(.width(4)) multiplexer_24 (.in1(4'b1100), .out(ALUCtr), .sel(or_9_out));  // open: in0, en
  or or_9 (or_9_out, and_18_out, comparator_31_eq);
  Comparator #(.width(6)) comparator_35 (.a(funct), .b(6'b100101), .eq(comparator_35_eq));  // open: gt, lt
  Comparator #(.width(6)) comparator_36 (.a(opcode), .b(6'b001101), .eq(comparator_36_eq));  // open: gt, lt
  Comparator #(.width(6)) comparator_37 (.a(funct), .b({6{1'b0}}), .eq(comparator_37_eq));  // open: gt, lt
  Comparator #(.width(6)) comparator_38 (.a(opcode), .b(6'b001111), .eq(LUI));  // open: gt, lt
  Comparator #(.width(6)) comparator_39 (.a(funct), .b(6'b000011), .eq(comparator_39_eq));  // open: gt, lt
  Comparator #(.width(6)) comparator_40 (.a(funct), .b(6'b000010), .eq(comparator_40_eq));  // open: gt, lt
  or or_10 (or_10_out, and_19_out, LUI);
  and and_19 (and_19_out, R_Type, or_11_out);
  or or_11 (or_11_out, comparator_41_eq, comparator_42_eq, comparator_43_eq);
  Comparator #(.width(6)) comparator_41 (.a(funct), .b({6{1'b0}}), .eq(comparator_41_eq));  // open: gt, lt
  Comparator #(.width(6)) comparator_42 (.a(funct), .b(6'b000010), .eq(comparator_42_eq));  // open: gt, lt
  Comparator #(.width(6)) comparator_43 (.a(funct), .b(6'b000011), .eq(comparator_43_eq));  // open: gt, lt
  and and_20 (and_20_out, comparator_35_eq, R_Type);
  or or_12 (or_12_out, and_20_out, comparator_36_eq);
  Multiplexer #(.width(4)) multiplexer_25 (.in1(4'b0000), .out(ALUCtr), .sel(or_13_out));  // open: in0, en
  and and_21 (and_21_out, comparator_37_eq, R_Type);
  or or_13 (or_13_out, and_21_out, LUI);
  Multiplexer #(.width(4)) multiplexer_26 (.in1(4'b0010), .out(ALUCtr), .sel(and_22_out));  // open: in0, en
  and and_22 (and_22_out, comparator_39_eq, R_Type);
  Multiplexer #(.width(4)) multiplexer_27 (.in1(4'b0001), .out(ALUCtr), .sel(and_23_out));  // open: in0, en
  and and_23 (and_23_out, comparator_40_eq, R_Type);
  Multiplexer multiplexer_28 (.in0(1'b0), .in1(1'b1), .out(Shift), .sel(or_10_out));  // open: en
  Multiplexer #(.width(4)) multiplexer_29 (.in1(4'b1010), .out(ALUCtr), .sel(or_12_out));  // open: in0, en

  // Other names for the same wires on the sheet: Store = MemWrite

  // Notes on the sheet:
  //   In
  //   R-Type
  //   "and" or "or"
  //   "and" or "or"
  //   Out
  //   I-Type
  //   Jump
  //   Jal
  //   Jal
  //   add
  //   addu
  //   sub
  //   subu
  //   Jr
  //   Branch
  //   Branch not Equal
  //   ALUCtrl
  //   slt
  //   sltu
  //   and
  //   Store
  //   load
  //   sll
  //   sra
  //   srl
  //   Shift
  //   or
endmodule
