// Logisim project regfile.circ as structural Verilog: 1 circuit, main circuit main
module main (
  input  [4:0] Read_Register_1,
  input  [4:0] Read_Register_2,
  input  [4:0] Write_Register,
  input  [31:0] Write_Data,
  input  Write_Enable,
  input  Clock,
  output [31:0] s0_Value,
  output [31:0] s1_Value,
  output [31:0] s2_Value,
  output [31:0] ra_Value,
  output [31:0] sp_Value,
  output [31:0] Read_Data_1,
  output [31:0] Read_Data_2
);

  wire i1, i2, i3, i4, i5, i6, i7, i8, i9, i10, i11, i12, i13, i14, i15, i16, i17, i18, i19, i20, i21, i22,
       i23, i24, i25, i26, i27, i28, i29, i30, i31;
  wire [31:0] o0, o1, o2, o3, o4, o5, o6, o7, o8, o9, o10, o11, o12, o13, o14, o15, o19, o20, o21, o22, o23,
       o24, o25, o26, o27, o28, o30;

  Multiplexer #(.select(5), .width(32)) multiplexer_1 (
    .in0(o0), .in1(o1), .in2(o2), .in3(o3), .in4(o4), .in5(o5), .in6(o6), .in7(o7), .in8(o8), .in9(o9),
    .in10(o10), .in11(o11), .in12(o12), .in13(o13), .in14(o14), .in15(o15), .in16(s0_Value), .in17(s1_Value),
    .in18(s2_Value), .in19(o19), .in20(o20), .in21(o21), .in22(o22), .in23(o23), .in24(o24), .in25(o25),
    .in26(o26), .in27(o27), .in28(o28), .in29(sp_Value), .in30(o30), .in31(ra_Value), .out(Read_Data_1),
    .sel(Read_Register_1));  // open: en
  Register #(.width(32)) zero (.Q(o0), .clk(Clock));  // open: D, en, clr
  Register #(.width(32)) at (.D(Write_Data), .en(i1), .Q(o1), .clk(Clock));  // open: clr
  Register #(.width(32)) s1 (.D(Write_Data), .en(i17), .Q(s1_Value), .clk(Clock));  // open: clr
  Register #(.width(32)) s0 (.D(Write_Data), .en(i16), .Q(s0_Value), .clk(Clock));  // open: clr
  Demultiplexer #(.select(5)) demultiplexer_1 (
    .out1(i1), .out2(i2), .out3(i3), .out4(i4), .out5(i5), .out6(i6), .out7(i7), .out8(i8), .out9(i9),
    .out10(i10), .out11(i11), .out12(i12), .out13(i13), .out14(i14), .out15(i15), .out16(i16), .out17(i17),
    .out18(i18), .out19(i19), .out20(i20), .out21(i21), .out22(i22), .out23(i23), .out24(i24), .out25(i25),
    .out26(i26), .out27(i27), .out28(i28), .out29(i29), .out30(i30), .out31(i31), .in(Write_Enable),
    .sel(Write_Register));  // open: out0, en
  Register #(.width(32)) v0 (.D(Write_Data), .en(i2), .Q(o2), .clk(Clock));  // open: clr
  Register #(.width(32)) s2 (.D(Write_Data), .en(i18), .Q(s2_Value), .clk(Clock));  // open: clr
  Register #(.width(32)) v1 (.D(Write_Data), .en(i3), .Q(o3), .clk(Clock));  // open: clr
  Register #(.width(32)) a0 (.D(Write_Data), .en(i4), .Q(o4), .clk(Clock));  // open: clr
  Register #(.width(32)) s3 (.D(Write_Data), .en(i19), .Q(o19), .clk(Clock));  // open: clr
  Register #(.width(32)) s4 (.D(Write_Data), .en(i20), .Q(o20), .clk(Clock));  // open: clr
  Register #(.width(32)) a1 (.D(Write_Data), .en(i5), .Q(o5), .clk(Clock));  // open: clr
  Register #(.width(32)) a2 (.D(Write_Data), .en(i6), .Q(o6), .clk(Clock));  // open: clr
  Register #(.width(32)) s6 (.D(Write_Data), .en(i22), .Q(o22), .clk(Clock));  // open: clr
  Register #(.width(32)) s5 (.D(Write_Data), .en(i21), .Q(o21), .clk(Clock));  // open: clr
  Register #(.width(32)) a3 (.D(Write_Data), .en(i7), .Q(o7), .clk(Clock));  // open: clr
  Register #(.width(32)) s7 (.D(Write_Data), .en(i23), .Q(o23), .clk(Clock));  // open: clr
  Register #(.width(32)) t0 (.D(Write_Data), .en(i8), .Q(o8), .clk(Clock));  // open: clr
  Register #(.width(32)) t1 (.D(Write_Data), .en(i9), .Q(o9), .clk(Clock));  // open: clr
  Register #(.width(32)) t8 (.D(Write_Data), .en(i24), .Q(o24), .clk(Clock));  // open: clr
  Register #(.width(32)) t9 (.D(Write_Data), .en(i25), .Q(o25), .clk(Clock));  // open: clr
  Multiplexer #(.select(5), .width(32)) multiplexer_2 (
    .in0(o0), .in1(o1), .in2(o2), .in3(o3), .in4(o4), .in5(o5), .in6(o6), .in7(o7), .in8(o8), .in9(o9),
    .in10(o10), .in11(o11), .in12(o12), .in13(o13), .in14(o14), .in15(o15), .in16(s0_Value), .in17(s1_Value),
    .in18(s2_Value), .in19(o19), .in20(o20), .in21(o21), .in22(o22), .in23(o23), .in24(o24), .in25(o25),
    .in26(o26), .in27(o27), .in28(o28), .in29(sp_Value), .in30(o30), .in31(ra_Value), .out(Read_Data_2),
    .sel(Read_Register_2));  // open: en
  Register #(.width(32)) t2 (.D(Write_Data), .en(i10), .Q(o10), .clk(Clock));  // open: clr
  Register #(.width(32)) k0 (.D(Write_Data), .en(i26), .Q(o26), .clk(Clock));  // open: clr
  Register #(.width(32)) t4 (.D(Write_Data), .en(i12), .Q(o12), .clk(Clock));  // open: clr
  Register #(.width(32)) t3 (.D(Write_Data), .en(i11), .Q(o11), .clk(Clock));  // open: clr
  Register #(.width(32)) gp (.D(Write_Data), .en(i28), .Q(o28), .clk(Clock));  // open: clr
  Register #(.width(32)) k1 (.D(Write_Data), .en(i27), .Q(o27), .clk(Clock));  // open: clr
  Register #(.width(32)) t6 (.D(Write_Data), .en(i14), .Q(o14), .clk(Clock));  // open: clr
  Register #(.width(32)) t5 (.D(Write_Data), .en(i13), .Q(o13), .clk(Clock));  // open: clr
  Register #(.width(32)) fp (.D(Write_Data), .en(i30), .Q(o30), .clk(Clock));  // open: clr
  Register #(.width(32)) sp (.D(Write_Data), .en(i29), .Q(sp_Value), .clk(Clock));  // open: clr
  Register #(.width(32)) t7 (.D(Write_Data), .en(i15), .Q(o15), .clk(Clock));  // open: clr
  Register #(.width(32)) ra (.D(Write_Data), .en(i31), .Q(ra_Value), .clk(Clock));  // open: clr

  // Other names for the same wires on the sheet: clk = Clock; o16[31:0] = s0_Value; o17[31:0] = s1_Value;
  //   o18[31:0] = s2_Value; o29[31:0] = sp_Value; o31[31:0] = ra_Value; read_data1[31:0] = Read_Data_1;
  //   read_data2[31:0] = Read_Data_2; read_reg1[4:0] = Read_Register_1; read_reg2[4:0] = Read_Register_2;
  //   write_en = Write_Enable; write_reg[4:0] = Write_Register

  // Notes on the sheet:
  //   INPUTS to your circuit
  //   DON'T CHANGE THE LOCATIONS OF THE INPUTS AND OUTPUTS!
  //   These are DEBUG/TEST outputs from your circuit.
  //   OUTPUTS from your circuit
endmodule
